# Fritzing sketch Untitled Sketch (saved by Fritzing 1.0.7)

parts:
  A1 = Esp32-c3 super mini
  OLED_SH1106_1_3″ = OLED 128x64 I2C Monochrome Display VDD-GND
  IMU_Sensor_BMI160 = BMI160 breakout
  AHT20_+_BMP280 = AHT20 BMP280 pressure and humidity breakout
  LiPo = LIPO-1000mAh [package=lipo-1000]
  TTP223B = TTP223B Capacitive Touch Sensor Module
  Buzzer = Piezo Speaker
  D1 = Diode [package=diode-hv]
  R1 = Resistor [tolerance=±5% power=0.25W resistance=100k package=THT]
  R2 = Resistor [tolerance=±5% power=0.25W resistance=100k package=THT]
  S1 = Toggle Switch [package=THT]
  TP4057_Charge_Module = TP4056 [chip_label=TP4056 package="DIP (Dual Inline) [THT]"]

nets:
  N1: A1.Pin_5, IMU_Sensor_BMI160.Pin_9, AHT20_+_BMP280.SCL
  N2: A1.Pin_10, Buzzer.pin2
  N3: A1.Pin_12, R1.Pin_1, R2.Pin_0
  N4: A1.Pin_13, TTP223B.SIG
  VDD: A1.Pin_14, OLED_SH1106_1_3″.VDD, IMU_Sensor_BMI160.Pin_7, IMU_Sensor_BMI160.Pin_12, AHT20_+_BMP280.VDD, TTP223B.VCC
  GND: A1.Pin_15, AHT20_+_BMP280.GND, TTP223B.GND, R2.Pin_1, TP4057_Charge_Module.OUT-
  N5: A1.Pin_16, S1.L2, TP4057_Charge_Module.+_in
  N6: OLED_SH1106_1_3″.SDA, IMU_Sensor_BMI160.Pin_10
  N7: IMU_Sensor_BMI160.Pin_8, IMU_Sensor_BMI160.Pin_11
  N8: LiPo.+, R1.Pin_0, TP4057_Charge_Module.B+
  N9: LiPo.-, TP4057_Charge_Module.B-
  N10: D1.A, TP4057_Charge_Module.OUT+
  N11: D1.C, S1.COM

custom parts:
  Esp32-c3 super mini: ESP32-C3 Development Board ESP32 SuperMini Development Board ESP32 Development Board WiFi Bluetooth.
  OLED 128x64 I2C Monochrome Display VDD-GND: OLED 128x64 I2C Monochrome Display. Note: there are two variants of this part, this one is the VDD GND SCK SDA variant. The other is GND VDD SCK SDA. Make sure you select the part that matches your module as using the incorrect part will probably destroy your module! In addition the mounting holes are marked on silkscreen but not by default drilled. If you want drilled mounting holes, copy a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
  BMI160 breakout: BMI160 Latest Stance Accelerometer Gyroscope module 6 Dof inertial Measurement Sensors.
  AHT20 BMP280 pressure and humidity breakout: Cheap breakout board for the BMP280, barometric pressure sensor, and AHT20, humidity sensor
  TTP223B Capacitive Touch Sensor Module: The TTP223B capacitive touch sensor module uses the TTP223B IC. The appropriate voltage is approximately 2 to 5.5 volts.
  TP4056: A DIP stand-in part for whatever IC you want. With 6 pins on a 300mil dual inline package (DIP) footprint.
